# Fritzing sketch motor (saved by Fritzing 0.9.3b)
breadboards: 1

parts:
  Raspberry_Pi1 = Raspberry Pi 2
  VCC1 = Battery block 9V
  M1 = DC Motor  # not connected

nets:
  N1: Raspberry_Pi1.GND, VCC1.-

notes:
  L9110S
  GND
  L9110S
  VCC
  L9110S
  A - 1B
  L9110S
  A - 1A
  L9110S
  Motor A
